// Digital circuit Microinstruction decoder.dig as structural Verilog
module Microinstruction_decoder (
  input  [15:0] Instruction,
  input  ALU_state,
  input  MOV_state,
  input  Ld_MAB_state,
  input  p_i_MP_state,
  input  LDi_state,
  input  LD_ST_direct_state,
  input  LD_ST__MP__state,
  input  Addr_arithm_state,
  input  misc_state,
  input  Fetch1_state,
  input  Fetch2_state,
  input  Fetch_int_state,
  input  EINT_mod,
  input  PushPC_mod,
  input  Jump_instr_mod,
  input  clk,
  input  [3:0] src_mod,
  input  [3:0] dest_mod,
  output [13:0] Select_bits,
  output [7:0] Enable_bits,
  output [11:0] Latch_bits,
  output Soft_int,
  output prefix,
  output clk_stop,
  output NOP,
  output [2:0] Function,
  output Const_enable,
  output Sub_Inv_Rev,
  output Arithm,
  output Enable_C_in_RotC,
  output nCMP,
  output Src1___eq__Dest
);

  wire and_1_out, and_2_out, and_3_out, and_4_out, and_5_out, and_6_out, and_7_out, and_8_out, and_9_out,
       and_10_out, and_11_out, and_12_out, and_13_out, and_14_out, and_15_out, and_16_out, and_17_out,
       and_18_out, and_19_out, and_20_out, and_21_out, and_22_out, and_27_out, and_28_out, and_29_out,
       and_30_out, and_31_out, and_32_out, and_33_out, and_34_out, and_35_out, and_36_out, and_37_out,
       and_38_out, and_39_out, and_40_out, and_41_out, and_42_out, and_43_out, and_44_out, and_45_out,
       and_46_out, and_47_out, and_48_out, and_49_out, and_50_out, and_51_out, and_52_out, and_53_out,
       and_54_out, and_55_out, and_56_out, and_57_out, and_58_out, and_59_out, and_60_out, and_61_out,
       and_66_out, CLIM, decoder_1_out_0, decoder_1_out_1, decoder_1_out_2, decoder_1_out_3, decoder_2_out_0,
       decoder_2_out_1, decoder_2_out_2, decoder_2_out_3, decoder_3_out_0, decoder_3_out_1, decoder_3_out_2,
       decoder_3_out_3, decoder_3_out_4, decoder_3_out_5, decoder_3_out_6, decoder_3_out_7, nand_1_out,
       nand_2_out, nand_3_out, nand_4_out, nand_5_out, nand_6_out, nand_7_out, nand_8_out, nand_9_out,
       nand_10_out, nand_11_out, nand_12_out, not_1_out, not_2_out, not_3_out, not_4_out, not_5_out,
       not_6_out, not_7_out, not_8_out, not_9_out, not_10_out, not_11_out, not_12_out, not_13_out,
       not_18_out, not_19_out, not_20_out, not_21_out, not_22_out, not_23_out, not_24_out, not_25_out,
       not_26_out, or_1_out, or_2_out, or_3_out, or_4_out, or_5_out, or_6_out, or_7_out, or_8_out, or_9_out,
       or_10_out, or_11_out, or_12_out, or_13_out, or_15_out, or_16_out, or_18_out, or_19_out, or_20_out,
       or_21_out, or_22_out, or_23_out, or_24_out, or_25_out, or_26_out, or_27_out, or_28_out, or_29_out,
       or_31_out, or_32_out, or_33_out, or_34_out, or_36_out, or_37_out, or_38_out, or_39_out, or_41_out,
       or_42_out, or_43_out, or_44_out, or_45_out, or_46_out, or_47_out, or_48_out, or_49_out, or_50_out,
       or_51_out, or_52_out, or_53_out, or_55_out, or_56_out, or_57_out, or_58_out, or_59_out, or_60_out,
       or_61_out, or_62_out, or_65_out, or_66_out, or_67_out, or_69_out, or_70_out, or_71_out, or_72_out,
       or_73_out, or_74_out, or_75_out, or_76_out, or_77_out, or_78_out, or_79_out, or_80_out, or_81_out,
       or_85_out, or_86_out, or_87_out, or_90_out, or_96_out, pulldown_1_out, pulldown_2_out, pulldown_3_out,
       pulldown_4_out, pulldown_5_out, pulldown_6_out, pulldown_7_out, pulldown_8_out, pulldown_9_out,
       pulldown_10_out, pulldown_11_out, pulldown_12_out, pulldown_15_out, pulldown_16_out, pulldown_17_out,
       pulldown_18_out, pulldown_19_out, pulldown_20_out, pulldown_21_out, pulldown_22_out, pulldown_23_out,
       pulldown_24_out, pulldown_25_out, pulldown_26_out, pulldown_27_out, pulldown_28_out, pulldown_29_out,
       pulldown_30_out, pulldown_31_out, pulldown_32_out, pulldown_33_out, pulldown_34_out, reset_pulse,
       SETIM;

  PullDown pulldown_1 (.out(pulldown_1_out));
  PullDown pulldown_2 (.out(pulldown_2_out));
  PullDown pulldown_3 (.out(pulldown_3_out));
  PullDown pulldown_4 (.out(pulldown_4_out));
  PullDown pulldown_5 (.out(pulldown_5_out));
  PullDown pulldown_6 (.out(pulldown_6_out));
  PullDown pulldown_7 (.out(pulldown_7_out));
  PullDown pulldown_8 (.out(pulldown_8_out));
  PullDown pulldown_9 (.out(pulldown_9_out));
  PullDown pulldown_10 (.out(pulldown_10_out));
  PullDown pulldown_11 (.out(pulldown_11_out));
  PullDown pulldown_12 (.out(pulldown_12_out));
  PullDown pulldown_13 (.out(Select_bits[12]));
  PullDown pulldown_14 (.out(Select_bits[13]));
  PullDown pulldown_15 (.out(pulldown_15_out));
  PullDown pulldown_16 (.out(pulldown_16_out));
  PullDown pulldown_17 (.out(pulldown_17_out));
  PullDown pulldown_18 (.out(pulldown_18_out));
  PullDown pulldown_19 (.out(pulldown_19_out));
  PullDown pulldown_20 (.out(pulldown_20_out));
  PullDown pulldown_21 (.out(pulldown_21_out));
  PullDown pulldown_22 (.out(pulldown_22_out));
  PullDown pulldown_23 (.out(pulldown_23_out));
  PullDown pulldown_24 (.out(pulldown_24_out));
  PullDown pulldown_25 (.out(pulldown_25_out));
  PullDown pulldown_26 (.out(pulldown_26_out));
  PullDown pulldown_27 (.out(pulldown_27_out));
  PullDown pulldown_28 (.out(pulldown_28_out));
  PullDown pulldown_29 (.out(pulldown_29_out));
  PullDown pulldown_30 (.out(pulldown_30_out));
  PullDown pulldown_31 (.out(pulldown_31_out));
  PullDown pulldown_32 (.out(pulldown_32_out));
  PullDown pulldown_33 (.out(pulldown_33_out));
  PullDown pulldown_34 (.out(pulldown_34_out));
  or or_1 (or_1_out, Fetch1_state, pulldown_5_out);
  or or_2 (or_2_out, Fetch1_state, pulldown_9_out);
  or or_3 (or_3_out, Fetch1_state, pulldown_20_out);
  or or_4 (or_4_out, Fetch1_state, pulldown_23_out);
  or or_5 (or_5_out, Fetch1_state, pulldown_28_out);
  or or_6 (or_6_out, Fetch1_state, pulldown_29_out);
  or or_7 (or_7_out, Fetch2_state, or_1_out);
  or or_8 (or_8_out, Fetch2_state, or_2_out);
  or or_9 (or_9_out, Fetch2_state, or_3_out);
  or or_10 (or_10_out, Fetch2_state, pulldown_21_out);
  or or_11 (or_11_out, Fetch2_state, or_5_out);
  or or_12 (or_12_out, Fetch2_state, or_6_out);
  or or_13 (or_13_out, Fetch2_state, pulldown_31_out);
  or or_14 (Select_bits[0], Fetch_int_state, pulldown_1_out);
  or or_15 (or_15_out, Fetch_int_state, or_9_out);
  or or_16 (or_16_out, Fetch_int_state, or_4_out);
  not not_1 (not_1_out, Instruction[11]);
  not not_2 (not_2_out, Instruction[13]);
  not not_3 (not_3_out, Instruction[14]);
  nand nand_1 (nand_1_out, not_2_out, not_3_out);
  or or_17 (Enable_bits[1], ALU_state, pulldown_16_out);
  or or_18 (or_18_out, ALU_state, pulldown_24_out);
  or or_19 (or_19_out, ALU_state, pulldown_25_out);
  not not_4 (not_4_out, Instruction[4]);
  Decoder #(.Selector_Bits(2)) decoder_1 (
    .sel(Instruction[1:0]), .out_0(decoder_1_out_0), .out_1(decoder_1_out_1), .out_2(decoder_1_out_2),
    .out_3(decoder_1_out_3));
  and and_1 (and_1_out, not_5_out, MOV_state, Instruction[3]);
  not not_5 (not_5_out, Instruction[2]);
  and and_2 (and_2_out, Instruction[2], MOV_state, Instruction[3]);
  not not_6 (not_6_out, src_mod[0]);
  not not_7 (not_7_out, dest_mod[0]);
  not not_8 (not_8_out, dest_mod[3]);
  nand nand_2 (nand_2_out, not_1_out, Instruction[3]);
  nand nand_3 (nand_3_out, not_1_out, not_4_out);
  and and_3 (and_3_out, src_mod[0], MOV_state);
  and and_4 (and_4_out, not_6_out, MOV_state);
  and and_5 (and_5_out, src_mod[1], MOV_state);
  and and_6 (and_6_out, src_mod[2], MOV_state);
  and and_7 (and_7_out, src_mod[3], MOV_state);
  and and_8 (and_8_out, not_7_out, Instruction[11], MOV_state);
  and and_9 (and_9_out, MOV_state, Instruction[11], dest_mod[0]);
  and and_10 (and_10_out, dest_mod[1], MOV_state);
  and and_11 (and_11_out, dest_mod[2], MOV_state);
  and and_12 (and_12_out, not_8_out, MOV_state);
  not not_9 (not_9_out, and_2_out);
  and and_13 (and_13_out, not_9_out, and_8_out);
  and and_14 (and_14_out, not_9_out, and_9_out);
  and and_15 (and_15_out, not_9_out, and_12_out);
  nand nand_4 (nand_4_out, not_1_out, nand_1_out);
  nand nand_5 (nand_5_out, not_1_out, nand_3_out);
  not not_10 (not_10_out, and_1_out);
  and and_16 (and_16_out, decoder_1_out_3, and_1_out);
  and and_17 (and_17_out, not_10_out, and_3_out);
  and and_18 (and_18_out, not_10_out, and_4_out);
  and and_19 (and_19_out, decoder_1_out_2, and_1_out);
  or or_20 (or_20_out, and_7_out, pulldown_2_out);
  or or_21 (or_21_out, and_6_out, pulldown_3_out);
  not not_11 (not_11_out, nand_4_out);
  not not_12 (not_12_out, nand_2_out);
  not not_13 (not_13_out, nand_3_out);
  or or_22 (or_22_out, and_5_out, pulldown_4_out);
  or or_23 (or_23_out, and_18_out, pulldown_15_out);
  nand nand_6 (nand_6_out, not_13_out, Instruction[3], nand_1_out);
  and and_20 (and_20_out, decoder_1_out_1, and_1_out);
  or or_24 (or_24_out, and_17_out, pulldown_18_out);
  or or_25 (or_25_out, and_15_out, or_18_out);
  or or_26 (or_26_out, and_10_out, pulldown_26_out);
  or or_27 (or_27_out, and_11_out, pulldown_27_out);
  nand nand_7 (nand_7_out, Instruction[3], not_4_out, ALU_state, not_11_out);
  and and_21 (and_21_out, decoder_1_out_3, and_2_out);
  or or_28 (or_28_out, and_14_out, or_11_out);
  or or_29 (or_29_out, and_13_out, or_12_out);
  nand nand_8 (nand_8_out, ALU_state, nand_7_out, not_12_out);
  nand nand_9 (nand_9_out, nand_6_out, ALU_state, Instruction[14]);
  nand nand_10 (nand_10_out, nand_6_out, ALU_state, Instruction[13]);
  and and_22 (and_22_out, decoder_1_out_2, and_2_out);
  or or_30 (Enable_bits[2], and_20_out, pulldown_17_out);
  or or_31 (or_31_out, and_19_out, pulldown_19_out);
  and and_23 (Arithm, ALU_state, Instruction[2]);
  and and_24 (Const_enable, ALU_state, Instruction[11]);
  and and_25 (Sub_Inv_Rev, Instruction[12], ALU_state);
  and and_26 (Function[2], ALU_state, nand_5_out);
  not not_14 (Function[1], nand_9_out);
  not not_15 (Function[0], nand_10_out);
  or or_32 (or_32_out, and_21_out, pulldown_33_out);
  not not_16 (nCMP, nand_7_out);
  not not_17 (Enable_C_in_RotC, nand_8_out);
  and and_27 (and_27_out, decoder_1_out_1, and_2_out);
  or or_33 (or_33_out, and_22_out, or_13_out);
  or or_34 (or_34_out, MOV_state, ALU_state);
  or or_35 (Select_bits[6], and_27_out, pulldown_7_out);
  or or_36 (or_36_out, and_27_out, or_19_out);
  not not_18 (not_18_out, or_34_out);
  or or_37 (or_37_out, not_18_out, Const_enable);
  not not_19 (not_19_out, or_37_out);
  or or_38 (or_38_out, Ld_MAB_state, pulldown_30_out);
  or or_39 (or_39_out, Ld_MAB_state, or_33_out);
  or or_40 (Src1___eq__Dest, and_59_out, Ld_MAB_state, not_19_out);
  or or_41 (or_41_out, Instruction[3], PushPC_mod);
  not not_20 (not_20_out, PushPC_mod);
  or or_42 (or_42_out, Instruction[4], PushPC_mod);
  and and_28 (and_28_out, Instruction[0], Ld_MAB_state);
  and and_29 (and_29_out, Instruction[1], Ld_MAB_state);
  and and_30 (and_30_out, Ld_MAB_state, Instruction[2]);
  not not_21 (not_21_out, Instruction[2]);
  and and_31 (and_31_out, not_21_out, Ld_MAB_state);
  and and_32 (and_32_out, not_20_out, Instruction[3]);
  and and_33 (and_33_out, Instruction[3], Ld_MAB_state, or_42_out);
  and and_34 (and_34_out, or_41_out, Ld_MAB_state);
  and and_35 (and_35_out, Ld_MAB_state, and_32_out);
  or or_43 (or_43_out, and_28_out, or_20_out);
  or or_44 (or_44_out, and_33_out, or_28_out);
  or or_45 (or_45_out, and_33_out, or_29_out);
  or or_46 (or_46_out, and_29_out, or_21_out);
  or or_47 (or_47_out, and_33_out, or_7_out);
  and and_36 (and_36_out, and_28_out, and_33_out);
  and and_37 (and_37_out, and_29_out, and_33_out);
  or or_48 (or_48_out, and_35_out, or_8_out);
  or or_49 (or_49_out, and_34_out, pulldown_10_out);
  or or_50 (or_50_out, and_31_out, or_23_out);
  or or_51 (or_51_out, and_30_out, or_31_out);
  or or_52 (or_52_out, and_36_out, or_26_out);
  or or_53 (or_53_out, and_37_out, or_27_out);
  or or_54 (Select_bits[7], LD_ST__MP__state, pulldown_8_out);
  or or_55 (or_55_out, LD_ST__MP__state, or_48_out);
  or or_56 (or_56_out, LD_ST__MP__state, pulldown_11_out);
  or or_57 (or_57_out, LD_ST__MP__state, or_38_out);
  or or_58 (or_58_out, LD_ST_direct_state, LD_ST__MP__state);
  not not_22 (not_22_out, dest_mod[0]);
  and and_38 (and_38_out, dest_mod[0], or_58_out);
  and and_39 (and_39_out, dest_mod[1], or_58_out);
  and and_40 (and_40_out, dest_mod[2], or_58_out);
  not not_23 (not_23_out, Instruction[12]);
  and and_41 (and_41_out, or_58_out, not_22_out);
  and and_42 (and_42_out, or_58_out, not_23_out);
  and and_43 (and_43_out, Instruction[12], or_58_out);
  or or_59 (or_59_out, and_39_out, or_43_out);
  or or_60 (or_60_out, and_40_out, or_46_out);
  or or_61 (or_61_out, and_39_out, or_52_out);
  or or_62 (or_62_out, and_40_out, or_53_out);
  or or_63 (Select_bits[3], and_38_out, or_22_out);
  or or_64 (Enable_bits[5], and_42_out, or_15_out);
  or or_65 (or_65_out, and_42_out, or_10_out);
  or or_66 (or_66_out, and_43_out, pulldown_22_out);
  or or_67 (or_67_out, and_43_out, pulldown_34_out);
  Decoder #(.Selector_Bits(2)) decoder_2 (
    .sel({Instruction[12], dest_mod[3]}), .out_0(decoder_2_out_0), .out_1(decoder_2_out_1),
    .out_2(decoder_2_out_2), .out_3(decoder_2_out_3));
  and and_44 (and_44_out, decoder_2_out_3, or_58_out);
  and and_45 (and_45_out, decoder_2_out_2, or_58_out);
  or or_68 (Enable_bits[3], and_44_out, or_24_out);
  or or_69 (or_69_out, and_45_out, or_50_out);
  and and_46 (and_46_out, and_38_out, decoder_2_out_1);
  or or_70 (or_70_out, and_46_out, or_44_out);
  and and_47 (and_47_out, and_41_out, decoder_2_out_1);
  or or_71 (or_71_out, and_47_out, or_45_out);
  and and_48 (and_48_out, decoder_2_out_0, or_58_out);
  or or_72 (or_72_out, and_48_out, or_25_out);
  or or_73 (or_73_out, LD_ST_direct_state, pulldown_12_out);
  and and_49 (and_49_out, Instruction[9], LDi_state);
  and and_50 (and_50_out, Instruction[10], LDi_state);
  not not_24 (not_24_out, Instruction[11]);
  or or_74 (or_74_out, LDi_state, pulldown_6_out);
  or or_75 (or_75_out, LDi_state, or_51_out);
  and and_51 (and_51_out, LDi_state, not_24_out);
  and and_52 (and_52_out, Instruction[11], LDi_state);
  or or_76 (or_76_out, and_52_out, or_70_out);
  or or_77 (or_77_out, and_52_out, or_71_out);
  or or_78 (or_78_out, and_51_out, or_72_out);
  or or_79 (or_79_out, and_49_out, or_61_out);
  or or_80 (or_80_out, and_50_out, or_62_out);
  and and_53 (and_53_out, Instruction[2], Addr_arithm_state);
  not not_25 (not_25_out, Instruction[8]);
  and and_54 (and_54_out, Instruction[8], Addr_arithm_state);
  and and_55 (and_55_out, Instruction[9], Addr_arithm_state);
  and and_56 (and_56_out, Instruction[10], Addr_arithm_state);
  or or_81 (or_81_out, p_i_MP_state, Addr_arithm_state);
  or or_82 (Select_bits[4], or_81_out, or_47_out);
  or or_83 (Select_bits[8], or_81_out, or_55_out);
  or or_84 (Select_bits[9], or_81_out, or_49_out);
  or or_85 (or_85_out, or_81_out, or_76_out);
  or or_86 (or_86_out, or_81_out, or_77_out);
  and and_57 (and_57_out, Addr_arithm_state, not_25_out);
  or or_87 (or_87_out, and_60_out, and_55_out);
  or or_88 (Select_bits[1], or_87_out, or_59_out);
  or or_89 (Latch_bits[3], or_87_out, or_79_out);
  not not_26 (not_26_out, and_53_out);
  or or_90 (or_90_out, and_61_out, and_56_out);
  or or_91 (Select_bits[2], or_90_out, or_60_out);
  or or_92 (Latch_bits[4], or_90_out, or_80_out);
  and and_58 (and_58_out, and_53_out, and_57_out);
  and and_59 (and_59_out, and_57_out, not_26_out);
  or or_93 (Select_bits[5], and_54_out, or_74_out);
  or or_94 (Enable_bits[0], and_59_out, or_69_out);
  or or_95 (Enable_bits[4], or_96_out, or_75_out);
  or or_96 (or_96_out, p_i_MP_state, and_58_out);
  and and_60 (and_60_out, Instruction[0], p_i_MP_state);
  and and_61 (and_61_out, Instruction[1], p_i_MP_state);
  Decoder #(.Selector_Bits(3)) decoder_3 (
    .sel(Instruction[10:8]), .out_0(decoder_3_out_0), .out_1(decoder_3_out_1), .out_2(decoder_3_out_2),
    .out_3(decoder_3_out_3), .out_4(decoder_3_out_4), .out_5(decoder_3_out_5), .out_6(decoder_3_out_6),
    .out_7(decoder_3_out_7));
  and and_62 (SETIM, misc_state, decoder_3_out_7);
  and and_63 (CLIM, misc_state, decoder_3_out_6);
  and and_64 (prefix, misc_state, decoder_3_out_5);
  and and_65 (Soft_int, misc_state, decoder_3_out_4);
  and and_66 (and_66_out, misc_state, decoder_3_out_3);
  or or_97 (Select_bits[10], and_66_out, or_56_out);
  or or_98 (Select_bits[11], and_66_out, or_73_out);
  and and_67 (reset_pulse, misc_state, decoder_3_out_2);
  and and_68 (clk_stop, misc_state, decoder_3_out_1);
  and and_69 (NOP, misc_state, decoder_3_out_0);
  nand nand_11 (nand_11_out, or_65_out, or_66_out);
  nand nand_12 (nand_12_out, or_65_out, or_66_out);
  and and_70 (Enable_bits[6], or_65_out, nand_11_out);
  and and_71 (Enable_bits[7], nand_12_out, or_66_out);
  and and_72 (Latch_bits[0], or_16_out, clk);
  and and_73 (Latch_bits[1], or_78_out, clk);
  and and_74 (Latch_bits[2], or_36_out, clk);
  and and_75 (Latch_bits[5], or_85_out, clk);
  and and_76 (Latch_bits[6], or_86_out, clk);
  and and_77 (Latch_bits[7], or_57_out, clk);
  and and_78 (Latch_bits[8], or_39_out, clk);
  and and_79 (Latch_bits[9], pulldown_32_out, clk);
  and and_80 (Latch_bits[10], or_32_out, clk);
  and and_81 (Latch_bits[11], or_67_out, clk);

  // Other names for the same wires on the sheet: EINT = EINT_mod; i0 = Instruction[0]; i1 = Instruction[1];
  //   i2 = Instruction[2]; i3 = Instruction[3]; i4 = Instruction[4]; i5 = Instruction[5]; i6 = Instruction[6];
  //   i7 = Instruction[7]; i8 = Instruction[8]; i9 = Instruction[9]; iA = Instruction[10]; iB = Instruction[11];
  //   iC = Instruction[12]; iD = Instruction[13]; iE = Instruction[14]; iF = Instruction[15];
  //   Jump_Instr = Jump_instr_mod; oAr = Arithm; oCMPi = nCMP; oConst_e = Const_enable; oEnCin = Enable_C_in_RotC;
  //   oF0 = Function[0]; oF1 = Function[1]; oF2 = Function[2]; oSub = Sub_Inv_Rev; push_PC = PushPC_mod

  // Notes on the sheet:
  //   src_mod: MOV source register address, 
  //   modified by sequencer
  //   dest_mod: MOV destination address
  //   LD/ST destination/source address
  //   modified by sequencer
  //   Arithm: Arythmetic shift (for SHR only)
  //   Enable_C_in_RotC: Use carry in for ADDC, SUBC, RORC, ROLC
  //   nCMP: Compare instruction, signal to prevent write to register
  //   Src1___eq__Dest: Use destination address also as a source address
  //   i0
  //   i1
  //   i2
  //   i3
  //   i4
  //   i5
  //   i6
  //   i7
  //   i8
  //   i9
  //   iA
  //   iB
  //   iC
  //   iD
  //   iE
  //   iF
  //   Microinstruction decoder
  //   S0
  //   S3_0
  //   S3_1
  //   S4
  //   S5
  //   S6
  //   S7
  //   S8
  //   S9_0
  //   S9_1
  //   S10_0
  //   S10_1
  //   S11
  //   S12
  //   E1
  //   E2
  //   E3
  //   E4
  //   E5
  //   E6
  //   T1
  //   T2
  //   L0
  //   L1
  //   L2
  //   LA3_0
  //   LA3_1
  //   L3
  //   L4
  //   L5
  //   L6
  //   L7
  //   L8
  //   W
  //   F1
  //   Fetch1
  //   Fetch states
  //   Fetch2
  //   F2
  //   F Int
  //   Fetch EInt
  //   Execute states
  //   ALU
  //   ALU state
  //   MOV
  //   MOV state
  //   Flags
  //   MDB
  //   IntV
  //   read special
  //   write to special
  //   IntV
  //   no rd
  //   ~i4
  //   ~iB
  //   i8 & iB
  //   ~i8 & iB
  //   rd SR
  //   rd MDB
  //   Int V base wr
  //   L2, S7
  //   SR wr
  //   MDB wr
  //   Load MAB
  //   Pre-increment
  //   MP addr b0
  //   MP addr b1
  //   offset src
  //   sel offset
  //   ~i2
  //   LD/ST (MP)
  //   T2
  //   W
  //   ~iC
  //   L3, L4
  //   LD/ST (address)
  //   LDi
  //   L3,L4
  //   Address Arithm
  //   S6 (add const to addr)
  //   ~i8 & ~i2
  //   ~i8 & i2
  //   E5 (add imm val to addr)
  //   E1, SnotD (add GPR to addr)
  //   MP post-increment
  //   Modifiers
  //   Codes for misc ops
  //   NOP just goes straight to Fetch1
  //   NOP
  //   HLT
  //   Reset
  //   Soft Interrupt
  //   Set Prefix
  //   Clear IM
  //   Set IM
  //   Sets a number of consecutive words that are to be loaded or stored
  //   Misc
  //   Pause
  //   Soft Interrupt has a step loading Interrupt #, and then goes straight to the EINT
  //   DMA sets address src selector to 0b11 and stops clock propagation into CPU
  //   Reset is a way to initiate reset sequence in software
  //   HLT severs clock signals
  //   DMA
endmodule
