// Digital circuit MultiWordEnabler.dig as structural Verilog
// This circuit substitues register addresses with counted ones for block transfers.
module MultiWordEnabler (
  input  clk,
  input  [15:0] Instr_in,
  input  block_size_Latch,
  input  load_cnt,
  input  \byte ,
  input  [1:0] word_cnt,
  output [15:0] instr_out,
  output Last,
  output Byte_2,
  output [3:0] prefix_indicator
);

  wire _2w, _4w, _8w, _16w, _74163_1_pin9, _74163_1_pin11, _74163_1_pin12, _74163_1_pin13, _74163_1_pin14,
       and_1_out, and_2_out, and_3_out, and_4_out, and_5_out, d_ff_as_1_q, d_ff_as_2_q, d_ff_as_3_q,
       multiplexer_1_out, multiplexer_2_out, multiplexer_3_out, multiplexer_4_out, not_1_out, not_2_out,
       not_4_out, not_5_out;

  not not_1 (not_1_out, word_cnt[0]);
  not not_2 (not_2_out, word_cnt[1]);
  and and_1 (and_1_out, not_1_out, not_2_out);
  and and_2 (and_2_out, word_cnt[0], not_2_out);
  and and_3 (and_3_out, not_1_out, word_cnt[1]);
  and and_4 (and_4_out, word_cnt[0], word_cnt[1]);
  Multiplexer multiplexer_1 (.sel(\byte ), .in_0(and_1_out), .in_1(and_2_out), .out(multiplexer_1_out));
  Multiplexer multiplexer_2 (.sel(\byte ), .in_0(and_2_out), .in_1(and_3_out), .out(multiplexer_2_out));
  Multiplexer multiplexer_3 (.sel(\byte ), .in_0(and_3_out), .in_1(and_4_out), .out(multiplexer_3_out));
  Multiplexer multiplexer_4 (.sel(\byte ), .in_0(and_4_out), .in_1(1'b0), .out(multiplexer_4_out));
  D_FF_AS d_ff_as_1 (
    .Set(1'b0), .D(multiplexer_1_out), .C(block_size_Latch), .Clr(and_5_out), .Q(d_ff_as_1_q));  // open: nQ
  D_FF_AS d_ff_as_2 (
    .Set(1'b0), .D(multiplexer_2_out), .C(block_size_Latch), .Clr(and_5_out), .Q(d_ff_as_2_q));  // open: nQ
  D_FF_AS d_ff_as_3 (
    .Set(1'b0), .D(multiplexer_3_out), .C(block_size_Latch), .Clr(and_5_out), .Q(d_ff_as_3_q));  // open: nQ
  D_FF_AS d_ff_as_4 (
    .Set(1'b0), .D(multiplexer_4_out), .C(block_size_Latch), .Clr(and_5_out), .Q(prefix_indicator[3]));  // open: nQ
  D_FF_AS byte__flag (.Set(1'b0), .D(\byte ), .C(block_size_Latch), .Clr(and_5_out), .Q(Byte_2));  // open: nQ
  or or_1 (prefix_indicator[2], d_ff_as_3_q, prefix_indicator[3]);
  or or_2 (prefix_indicator[1], d_ff_as_2_q, prefix_indicator[2]);
  _74163 _74163_1 (
    .pin1(1'b1), .pin2(clk), .pin3(_2w), .pin4(_4w), .pin5(_8w), .pin6(_16w), .pin7(1'b1), .pin8(1'b0),
    .pin9(_74163_1_pin9), .pin10(1'b1), .pin11(_74163_1_pin11), .pin12(_74163_1_pin12),
    .pin13(_74163_1_pin13), .pin14(_74163_1_pin14), .pin15(Last), .pin16(1'b1));
  not not_3 (_74163_1_pin9, load_cnt);
  or or_3 (prefix_indicator[0], d_ff_as_1_q, prefix_indicator[1]);
  not not_4 (not_4_out, Last);
  not not_5 (not_5_out, not_4_out);
  Multiplexer multiplexer_5 (.sel(prefix_indicator[0]), .in_0(Instr_in[5]), .in_1(_74163_1_pin14), .out(instr_out[5]));
  LED led_1 (.in(instr_out[5]));
  Multiplexer multiplexer_6 (.sel(prefix_indicator[1]), .in_0(Instr_in[6]), .in_1(_74163_1_pin13), .out(instr_out[6]));
  LED led_2 (.in(instr_out[6]));
  Multiplexer multiplexer_7 (.sel(prefix_indicator[2]), .in_0(Instr_in[7]), .in_1(_74163_1_pin12), .out(instr_out[7]));
  LED led_3 (.in(instr_out[7]));
  Multiplexer multiplexer_8 (.sel(prefix_indicator[3]), .in_0(Instr_in[4]), .in_1(_74163_1_pin11), .out(instr_out[4]));
  LED led_4 (.in(instr_out[4]));
  Multiplexer multiplexer_9 (.sel(prefix_indicator[0]), .in_0(Instr_in[8]), .in_1(_74163_1_pin14), .out(instr_out[8]));
  LED led_5 (.in(instr_out[8]));
  Multiplexer multiplexer_10 (.sel(prefix_indicator[1]), .in_0(Instr_in[9]), .in_1(_74163_1_pin13), .out(instr_out[9]));
  LED led_6 (.in(instr_out[9]));
  Multiplexer multiplexer_11 (
    .sel(prefix_indicator[2]), .in_0(Instr_in[10]), .in_1(_74163_1_pin12), .out(instr_out[10]));
  LED led_7 (.in(instr_out[10]));
  Multiplexer multiplexer_12 (
    .sel(prefix_indicator[3]), .in_0(Instr_in[11]), .in_1(_74163_1_pin11), .out(instr_out[11]));
  LED led_8 (.in(instr_out[11]));
  not not_6 (_2w, prefix_indicator[0]);
  not not_7 (_4w, prefix_indicator[1]);
  not not_8 (_8w, prefix_indicator[2]);
  not not_9 (_16w, prefix_indicator[3]);
  and and_5 (and_5_out, not_5_out, not_4_out);

  assign {instr_out[15:12], instr_out[3:0]} = {Instr_in[15:12], Instr_in[3:0]};

  // Notes on the sheet:
  //   Instr_in: Instruction word input
  //   block_size_Latch: latching signal, sinchronous with main clock
  //   Last: last word of the block
  //   load_cnt: clocked input for loading counter value
  //   byte: byte flag
  //   this is a standalone self-removing flag that makes LD/ST ops
  //    to work with individual bytes
  //   Byte_2: "byte" flag value
  //   Block size flags
  //   Multi-word transfer enabler
endmodule
