// Digital circuit ECM-16 computer.dig as structural Verilog
module ECM_16_computer (
  input  Clk,
  input  [31:0] in_2,
  input  [7:0] in_3,
  output [15:0] bus
);

  wire and_2_out, and_4_out, Byte, clk_stop, clk_t, E1, E2, E3, E4, E5, E6, Int_mock_out, Int_nq, Int_q, IRQ,
       L0, L1, L2, L3, L4, L5, L6, L7, L8, microinstruction_decoder_1_nop, nclk, nCMP, not_1_out, not_2_out,
       not_3_out, not_4_out, not_5_out, not_6_out, not_8_out, not_10_out, not_11_out, nr, or_1_out, prefix,
       pullup_2_out, R_out, RST, S0, S4, S5, S6, S7, S8, S11, S12, sequencer_1_addr_arithm_state,
       sequencer_1_alu_state, sequencer_1_eint_state, sequencer_1_fetch1_state, sequencer_1_fetch2_state,
       sequencer_1_fetch_int_state, sequencer_1_jsr_state, sequencer_1_jump_state, sequencer_1_ld_mab_state,
       sequencer_1_ld_st__mp__state, sequencer_1_ldd_std_state, sequencer_1_ldi_state,
       sequencer_1_misc_state, sequencer_1_mov_state, sequencer_1_p_i_mp_state, sequencer_1_push_pc_state,
       sequencer_1_sp_4_state, SnotD, Soft_Int, t_b_sel_1_bottom;
  wire [1:0] LA34, S3, S9, S10;
  wire [1:1] not_9_out;
  wire [3:0] dest_mod, main_alu_no_indicators_1_c, multiplexer_4_out, sequencer_1_prefix_ind, src_mod,
       Status_Register_flags_out;
  wire [6:0] ALU_signal;
  wire [7:0] _1_to_8b_extender_1_out, _1_to_8b_extender_2_out, clk_cnt, Instruction_Register_d_out,
       int_number_d_out, multiplexer_10_out;
  wire [7:6] en;
  wire [11:11] latch;
  wire [15:0] _1_to_16b_extender_1_out, _16MB_RAM_d, address_adder_1_out, address_adder_1_out_2,
       driver_1_out, IV_base_d_out, main_alu_no_indicators_1_output, MDB_d_out, MemPointers_mp_h,
       MemPointers_mp_l, multiplexer_1_out, multiplexer_2_out, multiplexer_3_out, multiplexer_5_out,
       multiplexer_6_out, pullup_1_out, register_file_no_display_1_src1_out,
       register_file_no_display_1_src1_to_bus, register_file_no_display_1_src2_out;
  wire [15:8] Instruction_Register_d_out_2;
  wire [31:0] BP, FP, MABH_d_out, multiplexer_7_out, multiplexer_8_out, multiplexer_9_out,
       multiplexer_11_out, PC, SP;
  wire [63:0] R0_3, R4_7;

  Seven_Seg_Hex seven_seg_hex_1 (.d(clk_cnt[7:4]), .dp(1'b0));
  not not_1 (not_1_out, nr);
  Multiplexer #(.Bits(16)) multiplexer_1 (
    .sel(S5), .in_0(driver_1_out), .in_1(address_adder_1_out), .out(multiplexer_1_out));
  Seven_Seg_Hex seven_seg_hex_2 (.d(clk_cnt[3:0]), .dp(1'b0));
  D_FF_AS Int (.Set(1'b0), .D(clk_stop), .C(clk_t), .Clr(not_1_out), .Q(Int_q), .nQ(Int_nq));
  _1_to_8b_extender _1_to_8b_extender_1 (.in(Instruction_Register_d_out[7]), .out(_1_to_8b_extender_1_out));
  Button Int_mock (.out(Int_mock_out));
  not not_2 (not_2_out, RST);
  Button #(.activeLow("true")) R (.out(R_out));
  LED led_1 (.in(Int_q));
  Multiplexer #(.Bits(16)) multiplexer_2 (
    .sel(S6), .in_0(driver_1_out), .in_1({_1_to_8b_extender_1_out, Instruction_Register_d_out}),
    .out(multiplexer_2_out));
  Multiplexer #(.Bits(16)) multiplexer_3 (
    .sel(S5), .in_0(multiplexer_2_out), .in_1(address_adder_1_out_2), .out(multiplexer_3_out));
  or or_1 (or_1_out, Soft_Int, Int_mock_out);
  not not_3 (not_3_out, S0);
  and and_1 (nr, not_2_out, R_out);
  Register_file_no_display register_file_no_display_1 (
    .Src2_out(register_file_no_display_1_src2_out), .Src1_out(register_file_no_display_1_src1_out), .nr(nr),
    .nCMP(nCMP), .L1(L1), .S1__eq_D(SnotD), .Dest(dest_mod[2:0]), .Src1(src_mod[3:1]),
    .Src2(Instruction_Register_d_out[2:0]), .D_in(driver_1_out), .R0_3(R0_3), .R4_7(R4_7),
    .Src1_to_bus(register_file_no_display_1_src1_to_bus));
  Main_ALU_no_indicators main_alu_no_indicators_1 (
    .Src2(register_file_no_display_1_src2_out), .Src1(register_file_no_display_1_src1_out),
    .Const(Instruction_Register_d_out), .Carry_in(Status_Register_flags_out[3]),
    .Const_enable(ALU_signal[0]), .Sub_Inv_Rev(ALU_signal[1]), .Arithm(ALU_signal[2]),
    .Enable_C_in_RotC(ALU_signal[3]), .Function(ALU_signal[6:4]), .Output(main_alu_no_indicators_1_output),
    .C(main_alu_no_indicators_1_c[3]), .O(main_alu_no_indicators_1_c[2]), .N(main_alu_no_indicators_1_c[1]),
    .Z(main_alu_no_indicators_1_c[0]));
  _1_to_16b_extender _1_to_16b_extender_1 (.in(multiplexer_2_out[15]), .out(_1_to_16b_extender_1_out));
  and and_2 (and_2_out, not_3_out, not_4_out);
  not not_4 (not_4_out, not_3_out);
  assign driver_1_out = E2 ? main_alu_no_indicators_1_output : 16'bz;  // Driver driver_1
  not not_5 (not_5_out, or_1_out);
  not not_6 (not_6_out, not_5_out);
  and and_3 (clk_t, Int_nq, Clk);
  Memory_Pointers MemPointers (
    .nr(nr), .LA34(LA34), .L3(L3), .L4(L4), .D3(multiplexer_3_out), .D4(multiplexer_1_out), .S3(S3), .PC(PC),
    .SP(SP), .FP(FP), .BP(BP), .MP_H(MemPointers_mp_h), .MP_L(MemPointers_mp_l));
  D_FF_AS Int_2 (.Set(1'b0), .D(or_1_out), .C(not_6_out), .Clr(and_2_out), .Q(IRQ));  // open: nQ
  not not_7 (nclk, clk_t);
  assign driver_1_out = E1 ? register_file_no_display_1_src1_to_bus : 16'bz;  // Driver driver_2
  LED u_clk (.in(clk_t));
  LED u_nclk (.in(nclk));
  PullUp #(.Bits(16)) pullup_1 (.out(pullup_1_out));
  LED led_2 (.in(IRQ));
  Seven_Seg_Hex seven_seg_hex_3 (.d(clk_cnt[7:4]), .dp(1'b0));
  not not_8 (not_8_out, nr);
  Seven_Seg_Hex seven_seg_hex_4 (.d(clk_cnt[3:0]), .dp(1'b0));
  Counter #(.Bits(8)) counter_1 (.en(nr), .C(clk_t), .clr(not_8_out), .out(clk_cnt));  // open: ovf
  Multiplexer #(.Bits(4)) multiplexer_4 (
    .sel(S7), .in_0(main_alu_no_indicators_1_c), .in_1(driver_1_out[3:0]), .out(multiplexer_4_out));
  assign driver_1_out = E4 ? multiplexer_5_out : 16'bz;  // Driver driver_3
  Multiplexer #(.Bits(16)) multiplexer_5 (
    .sel(S4), .in_0(MemPointers_mp_h), .in_1(MemPointers_mp_l), .out(multiplexer_5_out));
  LED led_3 (.in(R0_3[15]));
  LED led_4 (.in(R0_3[14]));
  LED led_5 (.in(R0_3[31]));
  LED led_6 (.in(R0_3[30]));
  LED led_7 (.in(R0_3[47]));
  LED led_8 (.in(R0_3[46]));
  LED led_9 (.in(R0_3[63]));
  LED led_10 (.in(R0_3[62]));
  LED led_11 (.in(R4_7[15]));
  LED led_12 (.in(R4_7[14]));
  LED led_13 (.in(R4_7[31]));
  LED led_14 (.in(R4_7[30]));
  LED led_15 (.in(R4_7[47]));
  LED led_16 (.in(R4_7[46]));
  LED led_17 (.in(R4_7[63]));
  LED led_18 (.in(R4_7[62]));
  LED led_19 (.in(R0_3[13]));
  LED led_20 (.in(R0_3[12]));
  LED led_21 (.in(R0_3[11]));
  LED led_22 (.in(R0_3[10]));
  LED led_23 (.in(R0_3[29]));
  LED led_24 (.in(R0_3[28]));
  LED led_25 (.in(R0_3[27]));
  LED led_26 (.in(R0_3[26]));
  LED led_27 (.in(R0_3[45]));
  LED led_28 (.in(R0_3[44]));
  LED led_29 (.in(R0_3[43]));
  LED led_30 (.in(R0_3[42]));
  LED led_31 (.in(R0_3[61]));
  LED led_32 (.in(R0_3[60]));
  LED led_33 (.in(R0_3[59]));
  LED led_34 (.in(R0_3[58]));
  LED led_35 (.in(R4_7[13]));
  LED led_36 (.in(R4_7[12]));
  LED led_37 (.in(R4_7[11]));
  LED led_38 (.in(R4_7[10]));
  LED led_39 (.in(R4_7[29]));
  LED led_40 (.in(R4_7[28]));
  LED led_41 (.in(R4_7[27]));
  LED led_42 (.in(R4_7[26]));
  LED led_43 (.in(R4_7[45]));
  LED led_44 (.in(R4_7[44]));
  LED led_45 (.in(R4_7[43]));
  LED led_46 (.in(R4_7[42]));
  LED led_47 (.in(R4_7[61]));
  LED led_48 (.in(R4_7[60]));
  LED led_49 (.in(R4_7[59]));
  LED led_50 (.in(R4_7[58]));
  LED led_51 (.in(Instruction_Register_d_out_2[15]));
  LED led_52 (.in(Instruction_Register_d_out_2[14]));
  LED led_53 (.in(Instruction_Register_d_out_2[13]));
  LED led_54 (.in(Instruction_Register_d_out_2[12]));
  Flags_Register_8bit Status_Register (
    .nR(nr), .Flags_in(multiplexer_4_out), .Clk(L2), .Flags_out(Status_Register_flags_out));
  LED led_55 (.in(R0_3[9]));
  LED led_56 (.in(R0_3[8]));
  LED led_57 (.in(R0_3[7]));
  LED led_58 (.in(R0_3[6]));
  LED led_59 (.in(R0_3[25]));
  LED led_60 (.in(R0_3[24]));
  LED led_61 (.in(R0_3[23]));
  LED led_62 (.in(R0_3[22]));
  LED led_63 (.in(R0_3[41]));
  LED led_64 (.in(R0_3[40]));
  LED led_65 (.in(R0_3[39]));
  LED led_66 (.in(R0_3[38]));
  LED led_67 (.in(R0_3[57]));
  LED led_68 (.in(R0_3[56]));
  LED led_69 (.in(R0_3[55]));
  LED led_70 (.in(R0_3[54]));
  LED led_71 (.in(R4_7[9]));
  LED led_72 (.in(R4_7[8]));
  LED led_73 (.in(R4_7[7]));
  LED led_74 (.in(R4_7[6]));
  LED led_75 (.in(R4_7[25]));
  LED led_76 (.in(R4_7[24]));
  LED led_77 (.in(R4_7[23]));
  LED led_78 (.in(R4_7[22]));
  LED led_79 (.in(R4_7[41]));
  LED led_80 (.in(R4_7[40]));
  LED led_81 (.in(R4_7[39]));
  LED led_82 (.in(R4_7[38]));
  LED led_83 (.in(R4_7[57]));
  LED led_84 (.in(R4_7[56]));
  LED led_85 (.in(R4_7[55]));
  LED led_86 (.in(R4_7[54]));
  Multiplexer #(.Bits(16)) multiplexer_6 (.sel(S0), .in_0(bus), .in_1(16'h1f01), .out(multiplexer_6_out));
  LED led_87 (.in(Instruction_Register_d_out_2[11]));
  LED led_88 (.in(Instruction_Register_d_out_2[10]));
  LED led_89 (.in(Instruction_Register_d_out_2[9]));
  LED led_90 (.in(Instruction_Register_d_out_2[8]));
  Multiplexer #(.Bits(32)) multiplexer_7 (
    .sel(S8), .in_0({MemPointers_mp_h, MemPointers_mp_l}), .in_1(MABH_d_out), .out(multiplexer_7_out));
  LED led_91 (.in(R0_3[5]));
  LED led_92 (.in(R0_3[4]));
  LED led_93 (.in(R0_3[3]));
  LED led_94 (.in(R0_3[2]));
  LED led_95 (.in(R0_3[21]));
  LED led_96 (.in(R0_3[20]));
  LED led_97 (.in(R0_3[19]));
  LED led_98 (.in(R0_3[18]));
  LED led_99 (.in(R0_3[37]));
  LED led_100 (.in(R0_3[36]));
  LED led_101 (.in(R0_3[35]));
  LED led_102 (.in(R0_3[34]));
  LED led_103 (.in(R0_3[53]));
  LED led_104 (.in(R0_3[52]));
  LED led_105 (.in(R0_3[51]));
  LED led_106 (.in(R0_3[50]));
  LED led_107 (.in(R4_7[5]));
  LED led_108 (.in(R4_7[4]));
  LED led_109 (.in(R4_7[3]));
  LED led_110 (.in(R4_7[2]));
  LED led_111 (.in(R4_7[21]));
  LED led_112 (.in(R4_7[20]));
  LED led_113 (.in(R4_7[19]));
  LED led_114 (.in(R4_7[18]));
  LED led_115 (.in(R4_7[37]));
  LED led_116 (.in(R4_7[36]));
  LED led_117 (.in(R4_7[35]));
  LED led_118 (.in(R4_7[34]));
  LED led_119 (.in(R4_7[53]));
  LED led_120 (.in(R4_7[52]));
  LED led_121 (.in(R4_7[51]));
  LED led_122 (.in(R4_7[50]));
  LED led_123 (.in(Instruction_Register_d_out[7]));
  LED led_124 (.in(Instruction_Register_d_out[6]));
  LED led_125 (.in(Instruction_Register_d_out[5]));
  LED led_126 (.in(Instruction_Register_d_out[4]));
  not not_9 (not_9_out[1], Byte);
  LED led_127 (.in(R0_3[1]));
  LED led_128 (.in(R0_3[0]));
  LED led_129 (.in(R0_3[17]));
  LED led_130 (.in(R0_3[16]));
  LED led_131 (.in(R0_3[33]));
  LED led_132 (.in(R0_3[32]));
  LED led_133 (.in(R0_3[49]));
  LED led_134 (.in(R0_3[48]));
  LED led_135 (.in(R4_7[1]));
  LED led_136 (.in(R4_7[0]));
  LED led_137 (.in(R4_7[17]));
  LED led_138 (.in(R4_7[16]));
  LED led_139 (.in(R4_7[33]));
  LED led_140 (.in(R4_7[32]));
  LED led_141 (.in(R4_7[49]));
  LED led_142 (.in(R4_7[48]));
  Register Instruction_Register (
    .nR(nr), .D_in(multiplexer_6_out), .Clk(L0),
    .D_out({Instruction_Register_d_out_2, Instruction_Register_d_out}));
  LED led_143 (.in(Instruction_Register_d_out[3]));
  LED led_144 (.in(Instruction_Register_d_out[2]));
  LED led_145 (.in(Instruction_Register_d_out[1]));
  LED led_146 (.in(Instruction_Register_d_out[0]));
  LED led_147 (.in(Status_Register_flags_out[0]));
  LED led_148 (.in(Status_Register_flags_out[1]));
  LED led_149 (.in(Status_Register_flags_out[2]));
  LED led_150 (.in(Status_Register_flags_out[3]));
  LED led_151 (.in(MABH_d_out[31]));
  Multiplexer #(.Bits(32)) multiplexer_8 (
    .sel(S11), .in_0(multiplexer_7_out), .in_1({IV_base_d_out, int_number_d_out, {8{1'b0}}}),
    .out(multiplexer_8_out));
  Multiplexer #(.Selector_Bits(2), .Bits(32)) multiplexer_9 (
    .sel(S9), .in_0({32{1'b0}}), .in_1({{30{1'b0}}, not_9_out[1], Byte}), .in_2(32'hfffffffc),
    .in_3({_1_to_16b_extender_1_out, multiplexer_2_out}), .out(multiplexer_9_out));
  LED led_152 (.in(MABH_d_out[30]));
  LED led_153 (.in(MABH_d_out[29]));
  LED led_154 (.in(MABH_d_out[28]));
  LED led_155 (.in(MABH_d_out[27]));
  LED led_156 (.in(PC[31]));
  LED led_157 (.in(PC[30]));
  LED led_158 (.in(PC[29]));
  LED led_159 (.in(PC[28]));
  LED led_160 (.in(SP[31]));
  LED led_161 (.in(SP[30]));
  LED led_162 (.in(SP[29]));
  LED led_163 (.in(SP[28]));
  LED led_164 (.in(FP[31]));
  LED led_165 (.in(FP[30]));
  LED led_166 (.in(FP[29]));
  LED led_167 (.in(FP[28]));
  LED led_168 (.in(BP[31]));
  LED led_169 (.in(BP[30]));
  LED led_170 (.in(BP[29]));
  LED led_171 (.in(BP[28]));
  Address_Adder address_adder_1 (
    .A(multiplexer_8_out), .B(multiplexer_9_out), .out({address_adder_1_out_2, address_adder_1_out}));  // open: Carry
  LED led_172 (.in(MABH_d_out[26]));
  LED led_173 (.in(MABH_d_out[25]));
  LED led_174 (.in(MABH_d_out[24]));
  LED led_175 (.in(MABH_d_out[23]));
  LED led_176 (.in(PC[27]));
  LED led_177 (.in(PC[26]));
  LED led_178 (.in(PC[25]));
  LED led_179 (.in(PC[24]));
  LED led_180 (.in(SP[27]));
  LED led_181 (.in(SP[26]));
  LED led_182 (.in(SP[25]));
  LED led_183 (.in(SP[24]));
  LED led_184 (.in(FP[27]));
  LED led_185 (.in(FP[26]));
  LED led_186 (.in(FP[25]));
  LED led_187 (.in(FP[24]));
  LED led_188 (.in(BP[27]));
  LED led_189 (.in(BP[26]));
  LED led_190 (.in(BP[25]));
  LED led_191 (.in(BP[24]));
  assign driver_1_out = E3 ? {{12{1'b0}}, Status_Register_flags_out} : 16'bz;  // Driver driver_4
  LED led_192 (.in(MABH_d_out[22]));
  LED led_193 (.in(MABH_d_out[21]));
  LED led_194 (.in(MABH_d_out[20]));
  LED led_195 (.in(MABH_d_out[19]));
  LED led_196 (.in(PC[23]));
  LED led_197 (.in(PC[22]));
  LED led_198 (.in(PC[21]));
  LED led_199 (.in(PC[20]));
  LED led_200 (.in(SP[23]));
  LED led_201 (.in(SP[22]));
  LED led_202 (.in(SP[21]));
  LED led_203 (.in(SP[20]));
  LED led_204 (.in(FP[23]));
  LED led_205 (.in(FP[22]));
  LED led_206 (.in(FP[21]));
  LED led_207 (.in(FP[20]));
  LED led_208 (.in(BP[23]));
  LED led_209 (.in(BP[22]));
  LED led_210 (.in(BP[21]));
  LED led_211 (.in(BP[20]));
  Sequencer sequencer_1 (
    .nR(nr), .Instruction({Instruction_Register_d_out_2, Instruction_Register_d_out}), .Clk(clk_t),
    .clk_stop(clk_stop), .prefix(prefix), .Interrupt(IRQ), .Status(Status_Register_flags_out),
    .src_mod(src_mod), .dest_mod(dest_mod), .Byte(Byte), .Fetch1_state(sequencer_1_fetch1_state),
    .Fetch2_state(sequencer_1_fetch2_state), .Fetch_int_state(sequencer_1_fetch_int_state),
    .ALU_state(sequencer_1_alu_state), .MOV_state(sequencer_1_mov_state),
    .Ld_MAB_state(sequencer_1_ld_mab_state), .LD_ST__MP__state(sequencer_1_ld_st__mp__state),
    .LDd_STd_state(sequencer_1_ldd_std_state), .LDi_state(sequencer_1_ldi_state),
    .Addr_arithm_state(sequencer_1_addr_arithm_state), .p_i_MP_state(sequencer_1_p_i_mp_state),
    .Jump_state(sequencer_1_jump_state), .SP_4_state(sequencer_1_sp_4_state),
    .Push_PC_state(sequencer_1_push_pc_state), .JSR_state(sequencer_1_jsr_state),
    .EINT_state(sequencer_1_eint_state), .misc_state(sequencer_1_misc_state),
    .Prefix_ind(sequencer_1_prefix_ind));
  Microinstruction_decoder microinstruction_decoder_1 (
    .clk(clk_t), .src_mod(src_mod), .dest_mod(dest_mod),
    .Instruction({Instruction_Register_d_out_2, Instruction_Register_d_out}),
    .Select_bits({S12, S11, S10, S9, S8, S7, S6, S5, S4, S3, S0}),
    .Enable_bits({en, E6, E5, E4, E3, E2, E1}),
    .Latch_bits({latch[11], L8, L7, L6, L5, L4, L3, LA34, L2, L1, L0}), .Soft_int(Soft_Int), .prefix(prefix),
    .RST(RST), .clk_stop(clk_stop), .NOP(microinstruction_decoder_1_nop), .Src1___eq__Dest(SnotD),
    .nCMP(nCMP), .Const_enable(ALU_signal[0]), .Sub_Inv_Rev(ALU_signal[1]), .Arithm(ALU_signal[2]),
    .Enable_C_in_RotC(ALU_signal[3]), .Function(ALU_signal[6:4]), .Fetch1_state(sequencer_1_fetch1_state),
    .Fetch2_state(sequencer_1_fetch2_state), .Fetch_int_state(sequencer_1_fetch_int_state),
    .ALU_state(sequencer_1_alu_state), .MOV_state(sequencer_1_mov_state),
    .Ld_MAB_state(sequencer_1_ld_mab_state), .LD_ST__MP__state(sequencer_1_ld_st__mp__state),
    .LD_ST_direct_state(sequencer_1_ldd_std_state), .LDi_state(sequencer_1_ldi_state),
    .Addr_arithm_state(sequencer_1_addr_arithm_state), .p_i_MP_state(sequencer_1_p_i_mp_state),
    .Jump_state(sequencer_1_jump_state), .SP_4_state(sequencer_1_sp_4_state),
    .Push_PC_state(sequencer_1_push_pc_state), .JSR_state(sequencer_1_jsr_state),
    .EINT_state(sequencer_1_eint_state), .misc_state(sequencer_1_misc_state));
  LED led_212 (.in(MABH_d_out[15]));
  LED led_213 (.in(MABH_d_out[18]));
  LED led_214 (.in(MABH_d_out[17]));
  LED led_215 (.in(MABH_d_out[16]));
  LED led_216 (.in(PC[19]));
  LED led_217 (.in(PC[18]));
  LED led_218 (.in(PC[17]));
  LED led_219 (.in(PC[16]));
  LED led_220 (.in(SP[19]));
  LED led_221 (.in(SP[18]));
  LED led_222 (.in(SP[17]));
  LED led_223 (.in(SP[16]));
  LED led_224 (.in(FP[19]));
  LED led_225 (.in(FP[18]));
  LED led_226 (.in(FP[17]));
  LED led_227 (.in(FP[16]));
  LED led_228 (.in(BP[19]));
  LED led_229 (.in(BP[18]));
  LED led_230 (.in(BP[17]));
  LED led_231 (.in(BP[16]));
  LED led_232 (.in(MABH_d_out[14]));
  LED led_233 (.in(MABH_d_out[13]));
  LED led_234 (.in(MABH_d_out[12]));
  LED led_235 (.in(MABH_d_out[11]));
  LED led_236 (.in(PC[15]));
  LED led_237 (.in(PC[14]));
  LED led_238 (.in(PC[13]));
  LED led_239 (.in(PC[12]));
  LED led_240 (.in(SP[15]));
  LED led_241 (.in(SP[14]));
  LED led_242 (.in(SP[13]));
  LED led_243 (.in(SP[12]));
  LED led_244 (.in(FP[15]));
  LED led_245 (.in(FP[14]));
  LED led_246 (.in(FP[13]));
  LED led_247 (.in(FP[12]));
  LED led_248 (.in(BP[15]));
  LED led_249 (.in(BP[14]));
  LED led_250 (.in(BP[13]));
  LED led_251 (.in(BP[12]));
  LED led_252 (.in(MABH_d_out[10]));
  LED led_253 (.in(MABH_d_out[9]));
  LED led_254 (.in(MABH_d_out[8]));
  LED led_255 (.in(MABH_d_out[7]));
  LED led_256 (.in(PC[11]));
  LED led_257 (.in(PC[10]));
  LED led_258 (.in(PC[9]));
  LED led_259 (.in(PC[8]));
  LED led_260 (.in(SP[11]));
  LED led_261 (.in(SP[10]));
  LED led_262 (.in(SP[9]));
  LED led_263 (.in(SP[8]));
  LED led_264 (.in(FP[11]));
  LED led_265 (.in(FP[10]));
  LED led_266 (.in(FP[9]));
  LED led_267 (.in(FP[8]));
  LED led_268 (.in(BP[11]));
  LED led_269 (.in(BP[10]));
  LED led_270 (.in(BP[9]));
  LED led_271 (.in(BP[8]));
  LED led_272 (.in(sequencer_1_prefix_ind[3]));
  LED led_273 (.in(sequencer_1_prefix_ind[2]));
  LED led_274 (.in(sequencer_1_prefix_ind[1]));
  Register MABH (.nR(nr), .D_in(address_adder_1_out), .Clk(L5), .D_out(MABH_d_out[15:0]));
  Register MABL (.nR(nr), .D_in(address_adder_1_out_2), .Clk(L5), .D_out(MABH_d_out[31:16]));
  LED led_275 (.in(MABH_d_out[6]));
  LED led_276 (.in(MABH_d_out[5]));
  LED led_277 (.in(MABH_d_out[4]));
  LED led_278 (.in(MABH_d_out[3]));
  LED led_279 (.in(PC[7]));
  LED led_280 (.in(PC[6]));
  LED led_281 (.in(PC[5]));
  LED led_282 (.in(PC[4]));
  LED led_283 (.in(SP[7]));
  LED led_284 (.in(SP[6]));
  LED led_285 (.in(SP[5]));
  LED led_286 (.in(SP[4]));
  LED led_287 (.in(FP[7]));
  LED led_288 (.in(FP[6]));
  LED led_289 (.in(FP[5]));
  LED led_290 (.in(FP[4]));
  LED led_291 (.in(BP[7]));
  LED led_292 (.in(BP[6]));
  LED led_293 (.in(BP[5]));
  LED led_294 (.in(BP[4]));
  LED led_295 (.in(sequencer_1_prefix_ind[0]));
  LED led_296 (.in(MDB_d_out[15]));
  LED led_297 (.in(MDB_d_out[14]));
  LED led_298 (.in(MDB_d_out[13]));
  LED led_299 (.in(MDB_d_out[12]));
  LED led_300 (.in(MABH_d_out[2]));
  LED led_301 (.in(MABH_d_out[1]));
  LED led_302 (.in(MABH_d_out[0]));
  LED led_303 (.in(PC[3]));
  LED led_304 (.in(PC[2]));
  LED led_305 (.in(PC[1]));
  LED led_306 (.in(PC[0]));
  LED led_307 (.in(SP[3]));
  LED led_308 (.in(SP[2]));
  LED led_309 (.in(SP[1]));
  LED led_310 (.in(SP[0]));
  LED led_311 (.in(FP[3]));
  LED led_312 (.in(FP[2]));
  LED led_313 (.in(FP[1]));
  LED led_314 (.in(FP[0]));
  LED led_315 (.in(BP[3]));
  LED led_316 (.in(BP[2]));
  LED led_317 (.in(BP[1]));
  LED led_318 (.in(BP[0]));
  LED led_319 (.in(MDB_d_out[11]));
  LED led_320 (.in(MDB_d_out[10]));
  LED led_321 (.in(MDB_d_out[9]));
  LED led_322 (.in(MDB_d_out[8]));
  LED led_323 (.in(MDB_d_out[7]));
  LED led_324 (.in(MDB_d_out[6]));
  LED led_325 (.in(MDB_d_out[5]));
  LED led_326 (.in(MDB_d_out[4]));
  LED led_327 (.in(microinstruction_decoder_1_nop));
  LED led_328 (.in(MDB_d_out[3]));
  LED led_329 (.in(MDB_d_out[2]));
  LED led_330 (.in(MDB_d_out[1]));
  LED led_331 (.in(MDB_d_out[0]));
  Multiplexer #(.Bits(8)) multiplexer_10 (
    .sel(S12), .in_0(Instruction_Register_d_out), .in_1(in_3), .out(multiplexer_10_out));
  Register MDB (.nR(nr), .D_in(driver_1_out), .Clk(L6), .D_out(MDB_d_out));
  Register IV_base (.nR(nr), .D_in(driver_1_out), .Clk(L8), .D_out(IV_base_d_out));
  Register_8bit int_number (.nR(nr), .D_in(multiplexer_10_out), .Clk(L7), .D_out(int_number_d_out));
  LED led_332 (.in(int_number_d_out[7]));
  LED led_333 (.in(int_number_d_out[6]));
  LED led_334 (.in(int_number_d_out[5]));
  LED led_335 (.in(int_number_d_out[4]));
  LED led_336 (.in(int_number_d_out[3]));
  LED led_337 (.in(int_number_d_out[2]));
  LED led_338 (.in(int_number_d_out[1]));
  assign driver_1_out = E5 ? MDB_d_out : 16'bz;  // Driver driver_5
  LED led_339 (.in(IV_base_d_out[15]));
  LED led_340 (.in(int_number_d_out[0]));
  _1_to_8b_extender _1_to_8b_extender_2 (.in(Instruction_Register_d_out[7]), .out(_1_to_8b_extender_2_out));
  LED led_341 (.in(IV_base_d_out[14]));
  LED led_342 (.in(IV_base_d_out[13]));
  LED led_343 (.in(IV_base_d_out[12]));
  LED led_344 (.in(IV_base_d_out[11]));
  LED led_345 (.in(S0));
  LED led_346 (.in(S3[0]));
  LED led_347 (.in(S3[1]));
  LED led_348 (.in(S4));
  LED led_349 (.in(S5));
  LED led_350 (.in(S6));
  LED led_351 (.in(S7));
  LED led_352 (.in(S8));
  LED led_353 (.in(S9[0]));
  LED led_354 (.in(S9[1]));
  LED led_355 (.in(S10[0]));
  LED led_356 (.in(S10[1]));
  LED led_357 (.in(S11));
  LED led_358 (.in(S12));
  assign driver_1_out = en[6] ? bus : 16'bz;  // Driver driver_6
  assign bus = en[7] ? driver_1_out : 16'bz;  // Driver driver_7
  LED led_359 (.in(IV_base_d_out[10]));
  LED led_360 (.in(IV_base_d_out[9]));
  LED led_361 (.in(IV_base_d_out[8]));
  LED led_362 (.in(IV_base_d_out[7]));
  LED led_363 (.in(IV_base_d_out[6]));
  LED led_364 (.in(IV_base_d_out[5]));
  LED led_365 (.in(IV_base_d_out[4]));
  LED led_366 (.in(IV_base_d_out[3]));
  LED led_367 (.in(IV_base_d_out[2]));
  LED led_368 (.in(IV_base_d_out[1]));
  LED led_369 (.in(IV_base_d_out[0]));
  Multiplexer #(.Selector_Bits(2), .Bits(32)) multiplexer_11 (
    .sel(S10), .in_0({MemPointers_mp_h, MemPointers_mp_l}), .in_1(MABH_d_out),
    .in_2({_1_to_8b_extender_2_out[6:0], Instruction_Register_d_out, MDB_d_out, 1'b0}), .in_3(in_2),
    .out(multiplexer_11_out));
  LED led_370 (.in(E1));
  LED led_371 (.in(E2));
  LED led_372 (.in(E3));
  LED led_373 (.in(E4));
  LED led_374 (.in(E5));
  LED u_E6 (.in(E6));
  LED led_375 (.in(en[6]));
  LED led_376 (.in(en[7]));
  T_B_sel t_b_sel_1 (.Flip(1'b0), .in(multiplexer_11_out[31:24]), .bottom(t_b_sel_1_bottom));  // open: top
  LED led_377 (.in(multiplexer_11_out[31]));
  LED led_378 (.in(multiplexer_11_out[30]));
  LED led_379 (.in(multiplexer_11_out[29]));
  LED led_380 (.in(multiplexer_11_out[28]));
  LED u_L0 (.in(L0));
  LED u_L1 (.in(L1));
  LED led_381 (.in(L2));
  LED led_382 (.in(LA34[0]));
  LED led_383 (.in(LA34[1]));
  LED led_384 (.in(L3));
  LED led_385 (.in(L4));
  LED led_386 (.in(L5));
  LED led_387 (.in(L6));
  LED led_388 (.in(L7));
  LED led_389 (.in(L8));
  LED W (.in(latch[11]));
  PullUp pullup_2 (.out(pullup_2_out));
  not not_10 (not_10_out, latch[11]);
  LED led_390 (.in(multiplexer_11_out[27]));
  LED led_391 (.in(multiplexer_11_out[26]));
  LED led_392 (.in(multiplexer_11_out[25]));
  LED led_393 (.in(multiplexer_11_out[24]));
  RAMSinglePortSel #(.AddrBits(23), .Bits(16)) _16MB_RAM (
    .A(multiplexer_11_out[23:1]), .CS(t_b_sel_1_bottom), .WE(latch[11]), .OE(not_10_out), .D(_16MB_RAM_d));
  LED led_394 (.in(multiplexer_11_out[23]));
  LED led_395 (.in(multiplexer_11_out[22]));
  LED led_396 (.in(multiplexer_11_out[21]));
  LED led_397 (.in(multiplexer_11_out[20]));
  not not_11 (not_11_out, latch[11]);
  LED led_398 (.in(multiplexer_11_out[19]));
  LED led_399 (.in(multiplexer_11_out[18]));
  LED led_400 (.in(multiplexer_11_out[17]));
  LED led_401 (.in(multiplexer_11_out[16]));
  and and_4 (and_4_out, latch[11], not_11_out);
  LED led_402 (.in(multiplexer_11_out[15]));
  LED led_403 (.in(multiplexer_11_out[14]));
  LED led_404 (.in(multiplexer_11_out[13]));
  LED led_405 (.in(multiplexer_11_out[12]));
  LED led_406 (.in(multiplexer_11_out[11]));
  LED led_407 (.in(multiplexer_11_out[10]));
  LED led_408 (.in(multiplexer_11_out[9]));
  LED led_409 (.in(multiplexer_11_out[8]));
  EEPROM #(.AddrBits(7), .Bits(16)) ROM (
    .A(multiplexer_11_out[7:1]), .CS(pullup_2_out), .WE(and_4_out), .OE(E6), .D(bus));
  LED led_410 (.in(multiplexer_11_out[7]));
  LED led_411 (.in(multiplexer_11_out[6]));
  LED led_412 (.in(multiplexer_11_out[5]));
  LED led_413 (.in(multiplexer_11_out[4]));
  LED led_414 (.in(multiplexer_11_out[3]));
  LED led_415 (.in(multiplexer_11_out[2]));
  LED led_416 (.in(multiplexer_11_out[1]));
  LED led_417 (.in(multiplexer_11_out[0]));
  Seven_Seg_Hex seven_seg_hex_5 (.d(clk_cnt[7:4]), .dp(1'b0));
  Seven_Seg_Hex seven_seg_hex_6 (.d(clk_cnt[3:0]), .dp(1'b0));

  // Other names for the same wires on the sheet: en[5:0] = {E6, E5, E4, E3, E2, E1}; T1 = en[6]; T2 = en[7];
  //   latch[10:0] = {L8, L7, L6, L5, L4, L3, LA34, L2, L1, L0}; W = latch[11];
  //   sel[13:0] = {S12, S11, S10, S9, S8, S7, S6, S5, S4, S3, S0}

  // Notes on the sheet:
  //   in_3: from interrupt controller
  //   Calculating core
  //   Fetch EINT === int ack
  //   Interrupt controller mock
  //   Const (8bit)
  //   Data bus (16bit)
  //   Flags (C,O,N,Z)
  //   ECM-16/TTL cpu
  //   Z
  //   N
  //   O
  //   C
  //   interrupt #
  //   NOP
  //   Data/Instr bus (16bit)
  //   S0
  //   S3_0
  //   S3_1
  //   S4
  //   S5
  //   S6
  //   S7
  //   S8
  //   S9_0
  //   S9_1
  //   S10_0
  //   S10_1
  //   S11
  //   S12
  //   DMA
  //   E1
  //   E2
  //   E3
  //   E4
  //   E5
  //   E6
  //   T1
  //   T2
  //   LA3_0
  //   LA3_1
  //   L0
  //   L1
  //   L2
  //   L3
  //   L4
  //   L5
  //   L6
  //   L7
  //   L8
  //   W
  //   contents of ROM (hex, n*v repeats v):
  //   2000,f,2100,1f,2200,3f,2300,7e,2400,fc,2500,1f8,2600,3f0,41f,112*0,1e
endmodule
